# Fritzing sketch circuit (saved by Fritzing 0.9.3b)
breadboards: 1

parts:
  Part1 = Arduino Uno (Rev3) - ICSP
  LCD1 = 20x4 LCD display [part_number=2004A]
  RHT1 = Humidity and Temperature Sensor RHT03
  R1 = Trimmer Potentiometer [maximum_resistance=10kΩ package=THT]
  Part2 = MQ-7 breakout

nets:
  N1: Part1.A0, Part2.DO
  N2: Part1.ICSP_MOSI, Part1.D11_PWM/MOSI, LCD1.E
  N3: Part1.D8, LCD1.DB6
  N4: Part1.D9_PWM, LCD1.DB5
  N5: Part1.D10_PWM/SS, LCD1.DB4
  N6: Part1.D12/MISO, LCD1.RS
  N7: Part1.D6_PWM, RHT1.Data-signal
  N8: Part1.D7, LCD1.DB7
  VCC: Part1.5V, LCD1.Vdd, LCD1.A_+, RHT1.Vcc, R1.leg2, Part2.VCC
  GND: Part1.GND, LCD1.Vss, LCD1.R/W, LCD1.K_-, RHT1.GND_2, R1.leg1, Part2.GND
  N9: LCD1.Vo, R1.wiper

custom parts:
  20x4 LCD display: 20x4 character display. CHECK LED POLARITY BEFORE CONNECTING POWER Some versions of the dispaly have the polarity of the LED pins "A" and "K" reversed.
  MQ-7 breakout: SKU: 101282
